# Fritzing sketch ESP8266_Kanji_Clock (saved by Fritzing 0.9.3b)

parts:
  Part1 = HUZZAH ESP8266 Breakout
  0x70 = 8x8 LED Matrix (red)
  0x72 = 8x8 LED Matrix (red)
  0x71 = 8x8 LED Matrix (red)
  0x73 = 8x8 LED Matrix (red)
  JACK1 = 2.1mm DC Barrel Jack
  S1 = Toggle Switch [package=THT]

nets:
  N1: Part1.VIN, JACK1.center
  N2: Part1.GND, 0x70.-, 0x72.-, 0x71.-, 0x73.-, JACK1.sleeve
  N3: Part1.GPIO16, S1.L2
  N4: Part1.GPIO14, S1.COM
  N5: Part1.GPIO12, S1.L1
  N6: Part1.3.3V, 0x70.+, 0x72.+, 0x71.+, 0x73.+
  N7: Part1.GPIO4, 0x70.D, 0x72.D, 0x71.D, 0x73.D
  N8: Part1.GPIO5, 0x70.C, 0x72.C, 0x71.C, 0x73.C

custom parts:
  HUZZAH ESP8266 Breakout: The ESP8266 processor from Espressif is an 80 MHz microcontroller with a full WiFi front-end (both as client and access point) and TCP/IP stack with DNS support as well.
  8x8 LED Matrix (red): 8x8 LED Matrix with I2C control (red)
  2.1mm DC Barrel Jack: 2.1mm DC Barrel Jack with Thru-Hole Connectors (breadboardable)
